# Fritzing sketch taiga_alarm_fritzing_schematic (saved by Fritzing 0.9.10b)
breadboards: 1

parts:
  M5Core-Ink = M5Core-Ink
  Infrared-Proximity-Sensor = Infrared Proximity Sensor [distance_to_obstacle=50%]
  U1 = SK6812 RGBW LED Strip

nets:
  5V: M5Core-Ink.1_5VIN
  3.3V: M5Core-Ink.2_3V3
  GND: M5Core-Ink.8_GND
  N1: M5Core-Ink.9_GND, U1.GND#0
  N2: M5Core-Ink.10_5V, U1.+5V
  N3: M5Core-Ink.13_G25, Infrared-Proximity-Sensor.Vout
  N4: M5Core-Ink.15_G26, U1.Din, U1.GND#3
  N5: M5Core-Ink.23_3V3, Infrared-Proximity-Sensor.Vcc
  N6: M5Core-Ink.28_GND, Infrared-Proximity-Sensor.GND

notes:
  Microprocessor (ESP32)
  Inputs (Sensors)
  M5Stack Modules
  Outputs (Actuators)

custom parts:
  M5Core-Ink: M5Stack Core Ink ESP32 Board
  SK6812 RGBW LED Strip: SK6812 RGBW Strip
